// Logisim project bfc.circ as structural Verilog: 7 circuits, main circuit comp
module main (
  input  in_1,
  input  [3:0] in_2,
  input  [7:0] in_3,
  input  in_4,
  input  in_5,
  output out_6,
  output out_7,
  output out_8,
  output out_9,
  output [7:0] out_10,
  output out_11,
  output out_12,
  output out_13,
  output out_14,
  output out_15
);

  wire and_1_out, and_2_out, and_3_out, and_4_out, and_5_out, comparator_1_eq, d_ff_1_q,
       demultiplexer_2_out6, demultiplexer_2_out7, lpcont_1_out_4, lpcont_2_out_4, nor_1_out, not_1_out,
       or_1_out, or_2_out;

  and and_1 (and_1_out, in_1, ~d_ff_1_q);  // AND_Gate
  Demultiplexer #(.enable("false")) demultiplexer_1 (.out0(out_7), .out1(out_6), .in(and_1_out), .sel(lpcont_2_out_4));
  D_Flip_Flop #(.trigger("high")) d_ff_1 (
    .clk(or_1_out), .D(or_1_out), .Q(d_ff_1_q), .reset(in_4));  // open: Qn, preset, en
  or or_1 (or_1_out, out_13, in_2[3], out_14);
  nor nor_1 (nor_1_out, out_7, or_2_out);
  or or_2 (or_2_out, lpcont_2_out_4, lpcont_1_out_4);
  not not_1 (not_1_out, and_1_out);
  Demultiplexer #(.select(3), .enable("false")) demultiplexer_2 (
    .out6(demultiplexer_2_out6), .out7(demultiplexer_2_out7), .in(not_1_out), .sel(in_2[2:0]));  // open: out0, out1, out2, out3, out4, out5
  CMPs cmps_1 (
    .in_1(nor_1_out), .in_2(in_2[2:0]), .out_3(out_8), .out_4(out_9), .out_5(out_11), .out_6(out_12),
    .out_7(out_13), .out_8(out_14));  // open: out_9, out_10
  and and_2 (and_2_out, lpcont_1_out_4, demultiplexer_2_out7);
  and and_3 (and_3_out, lpcont_2_out_4, demultiplexer_2_out6);
  Comparator comparator_1 (.a(in_3), .b({8{1'b0}}), .eq(comparator_1_eq));  // open: gt, lt
  and and_4 (and_4_out, comparator_1_eq, demultiplexer_2_out6);
  and and_5 (and_5_out, ~comparator_1_eq, demultiplexer_2_out7);  // AND_Gate
  lpCont lpcont_1 (.in_1(and_2_out), .in_2(and_4_out), .out_4(lpcont_1_out_4), .in_3(in_5));
  lpCont lpcont_2 (.in_1(and_3_out), .in_2(and_5_out), .out_4(lpcont_2_out_4), .in_3(in_5));

  assign out_10 = in_3;
  assign out_15 = in_2[3];
endmodule

module ROM (
  input  in_1,
  input  in_2,
  input  in_3,
  output [3:0] out_4
);

  wire or_1_out;
  wire [10:0] counter_1_q;

  Counter #(.width(11), .max('h7ff)) counter_1 (
    .load(in_1), .Q(counter_1_q), .clk(or_1_out), .clr(in_3));  // open: D, count, carry
  or or_1 (or_1_out, in_1, in_2);
  ROM_part #(.addrWidth(11), .dataWidth(4)) rom_1 (.addr(counter_1_q), .data(out_4));  // open: sel

  // Notes on the sheet:
  //   contents of rom_1 (hex, n*v repeats v):
  //   10*2 6 3 0 10*2 0 11*2 0 2 2 2 1 1 1 7 0 2 4 0 4 6*2 4 1 4 0 3 3 4 0 2 2 4 1 4*3 4 7*2 4 8*3 4 1 3 3
  //   3 4 2 2 2 4 6 3 7 0 5*2 4 2 2 6 3 3 1 2 0 7 1 4 6 3 7 0 0 4 6 3 7 1 1 1 2 0 0 3 0 5 4 10*3 6 3 3 0
  //   6*2 6 3 1 6*3 0 7 1 6 3 0 2 0 2 1 1 7 1 2 0 2 5*0 5 4 10*3 7 6*1 6 5*1 7 0 3 1 1 1 6 7*0 6 1 1 6 3 0
  //   0 6 5*0 7 1 2 4*1 6 5*1 7 0 0 0 7 0 0 6 5*0 7 1 1 6 3 1 1 1 6 5*1 7 0 0 0 2 0 0 6 5*0 7 1 1 7 0 6 3
  //   1 2 0 7 4*1 3 5*1 6 5*1 7 5*0 6 3 7 5*0 7 4*1 6 5*1 7 1 1 2 7*0 6 1 2 6*0 7 1 2 6 3 1 1 6 3 0 2 0 2
  //   1 1 7 1 6 3 0 2 0 3 1 1 7 0 6 3 1 2 0 7 0 0 6 3 1 1 2 0 0 7 1 6 6 3 7 1 1 1 6 5*1 7 1 1 6 3 7 6*0 6
  //   5*0 7 1 7 4*1 7 1 6 3 1 3 0 7 1 6 8*0 6 1 1 8*2 6 3 1 6*2 0 7 1 4 8*0 7 8*2 6 3 1 5*2 1 4*2 1 6*2 0
  //   0 0 7 1 1 1 4 0 4 0 2 2 2 4 1 4 1 4 0 0 5*2 6 3 1 1 3 0 0 7 1 6 3 7 1 1 1 6 1 1 1 4 0 8*2 6 3 1 6*3
  //   0 7 1 1 1 7 10*2 6 3 1 2 2 2 1 6*2 0 0 7 1 2 2 4 1 2 4 6 3 7 0 4 6 3 7 6*0 6 5*0 7 2 6 5*1 7 5*0 6 1
  //   1 1 6 3 1 2 0 7 0 2 1 1 6 0 0 3 1 1 6 3 0 2 1 7 7 0 6 3 1 2 0 7 0 6 0 0 3 1 1 3 7 1 9*2 6 0 0 2 1 1
  //   3 1 3 6 0 0 0 3 1 1 1 6 3 0 0 2 1 1 7 7 0 0 6 3 1 1 2 0 0 7 0 6 3 0 6 3 7 1 7 1 1 7 1 3 0 0 0 2 0 6
  //   3 1 3 0 0 2 1 7 2 1 6 3 1 1 1 10*2 0 0 0 7 6*0 7 5*1 6 3 7 0 6 3 1 2 0 0 2 1 7 0 6 3 1 2 0 7 7*1 6
  //   5*1 7 5*0 6 5*0 7 5*1 6 0 6 3 0 2 0 2 0 2 1 1 1 7 0 0 6 3 1 1 2 0 0 7 8*2 6 3 0 6*2 1 7 0 4 6 3 7
  //   9*1 7 0 6 3 0 2 0 2 0 2 1 1 1 7 0 0 6 3 1 1 2 0 0 7 8*2 6 3 0 6*2 1 7 0 4 6 3 7 0 6 5*0 7 5*1 6 1 2
  //   4*1 7 1 1 1 9*2 4 9*3 0 2 1 3 7 0 6 3 1 2 0 7 1 7 10*2 6 3 0 8*2 0 11*2 0 6*2 1 1 1 7 0 4 1 4*2 6 3
  //   0 4*2 1 7 0 2 4 0 3 3 4 3 3 3 4 5*2 4 1 2 2 2 4 0 4*2 4 3 3 3 4 3 3 4 1 2 4 0 0 3 3 4 2 2 6 3 3 1 1
  //   1 2 0 0 0 7 1 1 1 2 2 4 0 0 0 2 6 0 0 0 8*2 6 3 1 6*2 0 7 1 4 0 0 0 7 10*2 4 f 1 1 7 1 1 6 1 1 7 7 1
  //   7 0 6 3 0 0 6 0 0 7 0 0 6 0 0 7 1 1 3 1 1 6 1 1 7 1 1 6 1 1 7 7 1 7 0 6 3 0 0 6 0 0 7 0 0 6 0 0 7 2
  //   6 1 1 7 1 1 6 1 1 7 7 1 7 0 6 3 0 0 6 0 0 7 0 0 6 0 0 7 1 6 0 2 0 0 2 1 1 1 3 7 0 6 1 2 0 3 7 0 0 6
  //   1 1 2 0 0 6 3 7 7 2 1 1 6 0 0 3 1 1 3 7 0 0 6 1 1 2 4*0 2 1 1 3 7 0 0 6 1 1 2 0 0 3 7 1 1 6 0 0 2 1
  //   1 3 7 2 0 0 6 1 1 3 0 0 3 7 4*1 6 3 1 1 6 1 1 7 1 1 6 1 1 7 5*1 2 2 0 0 7 0 0 6 3 6*1 6 1 1 7 1 1 6
  //   1 1 7 1 7 0 7 1 7 0 6 3 0 0 6 0 0 7 0 0 6 0 0 7 1 6 0 2 0 0 2 1 1 1 3 7 0 6 6 1 2 0 3 7 0 0 6 3 7 2
  //   1 1 7 0 0 6 1 1 2 4*0 2 1 1 3 7 0 0 6 1 1 2 0 0 3 7 1 1 6 0 0 2 1 1 3 7 2 0 0 6 1 1 3 0 0 3 7 4*1 6
  //   3 1 1 6 1 1 7 1 1 6 1 1 7 5*1 2 0 0 7 0 0 6 3 6*1 6 1 1 7 1 1 6 1 1 7 1 7 0 7 0 6 1 2 0 3 7 6*1 6 0
  //   0 2 1 1 3 6 3 0 0 3 0 0 2 6 0 0 0 6 3 1 2 0 0 2 1 7 2 1 3 6 3 6 6 3 7 0 3 1 7 0 6 3 1 1 1 2 0 0 0 7
  //   1 7 0 6 3 1 1 1 3 0 0 0 7 0 6 3 1 2 0 7 4*1 6 0 0 2 1 1 3 7 0 0 7 6*1 7 0 0 6 3 1 1 2 6 0 0 0 6 3 1
  //   2 0 0 2 1 7 2 1 3 6 3 6 6 3 7 0 3 1 7 0 6 3 1 1 1 3 0 0 0 7 1 7 0 6 3 1 1 1 2 0 0 0 7 0 6 3 1 2 0 7
  //   4*1 6 1 1 2 0 0 3 7 1 1 7 7 7 7*0 7 0 7 0 0 6 3 6*1 6 1 1 7 1 1 6 1 1 7 1 7 0 7 0 6 1 2 0 3 7 6*1 6
  //   0 0 2 1 1 3 6 3 0 0 3 0 0 2 6 0 0 0 6 3 1 2 0 0 2 1 7 2 1 3 6 3 6 6 3 7 0 3 1 7 0 6 3 1 1 1 2 0 0 0
  //   7 1 7 0 6 3 1 1 1 3 0 0 0 7 0 6 3 1 2 0 7 4*1 6 0 0 2 1 1 3 7 0 0 7 6*1 7 0 0 6 3 1 1 2 6 0 0 0 6 3
  //   1 2 0 0 2 1 7 2 1 3 6 3 6 6 3 7 0 3 1 7 0 6 3 1 1 1 3 0 0 0 7 1 7 0 6 3 1 1 1 2 0 0 0 7 0 6 3 1 2 0
  //   7 4*1 6 1 1 2 0 0 3 7 1 1 7 7 7 7*0 7 f
endmodule

module RAM (
  input  in_1,
  input  in_2,
  input  in_3,
  input  [7:0] in_4,
  input  in_5,
  input  in_6,
  input  in_7,
  output [7:0] out_8
);

  wire buffer_1_out, buffer_2_out, buffer_3_out, buffer_4_out, nor_1_out, not_2_out, or_1_out, or_2_out;
  wire [1:1] not_1_out;
  wire [7:0] adder_1_out, multiplexer_1_out, multiplexer_2_out;
  wire [11:0] counter_1_q;

  buf buffer_1 (buffer_1_out, in_2);
  buf buffer_2 (buffer_2_out, buffer_1_out);
  buf buffer_3 (buffer_3_out, buffer_2_out);
  buf buffer_4 (buffer_4_out, buffer_3_out);
  Counter #(.width(12), .max('hfff)) counter_1 (
    .load(buffer_4_out), .Q(counter_1_q), .clk(nor_1_out), .clr(in_3));  // open: D, count, carry
  nor nor_1 (nor_1_out, in_1, in_2);
  Multiplexer #(.width(8), .enable("false")) multiplexer_1 (
    .in0(adder_1_out), .in1(in_4), .out(multiplexer_1_out), .sel(in_5));
  or or_1 (or_1_out, in_1, in_2, in_6, in_7);
  not not_1 (not_1_out[1], nor_1_out);
  not not_2 (not_2_out, or_2_out);
  or or_2 (or_2_out, in_5, or_1_out);
  RAM_part #(.addrWidth(12), .bus("separate")) ram_1 (
    .addr(counter_1_q), .din(multiplexer_1_out), .data(out_8), .clk(not_2_out), .clr(in_3));  // open: str, sel, ld
  Multiplexer #(.select(2), .width(8), .enable("false")) multiplexer_2 (
    .in0(8'h1), .in1({8{1'b1}}), .in2({8{1'b0}}), .in3({8{1'b0}}), .out(multiplexer_2_out),
    .sel({not_1_out[1], in_7}));
  Adder adder_1 (.a(out_8), .b(multiplexer_2_out), .out(adder_1_out));  // open: cin, cout
endmodule

module CMPs (
  input  in_1,
  input  [2:0] in_2,
  output out_3,
  output out_4,
  output out_5,
  output out_6,
  output out_7,
  output out_8,
  output out_9,
  output out_10
);

  wire buffer_1_out, buffer_2_out, buffer_3_out, buffer_4_out, buffer_5_out, buffer_6_out, buffer_7_out,
       decoder_1_out0, decoder_1_out1, decoder_1_out2, decoder_1_out3, decoder_1_out4, decoder_1_out5,
       decoder_1_out6, decoder_1_out7;

  Decoder #(.select(3), .enable("false")) decoder_1 (
    .out0(decoder_1_out0), .out1(decoder_1_out1), .out2(decoder_1_out2), .out3(decoder_1_out3),
    .out4(decoder_1_out4), .out5(decoder_1_out5), .out6(decoder_1_out6), .out7(decoder_1_out7), .sel(in_2));
  buf buffer_1 (buffer_1_out, buffer_2_out);
  buf buffer_2 (buffer_2_out, buffer_3_out);
  buf buffer_3 (buffer_3_out, buffer_4_out);
  buf buffer_4 (buffer_4_out, buffer_5_out);
  buf buffer_5 (buffer_5_out, buffer_6_out);
  buf buffer_6 (buffer_6_out, buffer_7_out);
  buf buffer_7 (buffer_7_out, in_1);
  and and_1 (out_3, decoder_1_out0, buffer_1_out);
  and and_2 (out_4, decoder_1_out1, buffer_2_out);
  and and_3 (out_5, decoder_1_out2, buffer_3_out);
  and and_4 (out_6, decoder_1_out3, buffer_4_out);
  and and_5 (out_7, decoder_1_out4, buffer_5_out);
  and and_6 (out_8, decoder_1_out5, buffer_6_out);
  and and_7 (out_9, decoder_1_out6, buffer_7_out);
  and and_8 (out_10, decoder_1_out7, in_1);
endmodule

module lpCont (
  input  in_1,
  input  in_2,
  input  in_3,
  output out_4
);

  wire comparator_1_eq, or_1_out;
  wire [5:0] counter_1_q;

  or or_1 (or_1_out, in_1, in_2);
  Counter #(.width(6), .max('h3f)) counter_1 (
    .load(in_1), .Q(counter_1_q), .clk(or_1_out), .clr(in_3));  // open: D, count, carry
  Comparator #(.width(6)) comparator_1 (.a(counter_1_q), .b({6{1'b0}}), .eq(comparator_1_eq));  // open: gt, lt
  not not_1 (out_4, comparator_1_eq);
endmodule

module Proc (
  input  in_1,
  input  in_2,
  input  [6:0] in_3,
  input  in_4,
  output [6:0] out_5,
  output out_6,
  output out_7,
  output out_8,
  output out_9,
  output out_10,
  output out_11
);

  wire main_1_out_6, main_1_out_7, main_1_out_8, main_1_out_9, main_1_out_11, main_1_out_12, or_1_out;
  wire [3:0] rom_1_out_4;
  wire [7:0] bit_extender_1_out, ram_1_out_8;
  wire [7:7] main_1_out_10;

  or or_1 (or_1_out, in_2, out_8, out_6);
  main main_1 (
    .in_1(in_1), .in_5(in_2), .out_10({main_1_out_10[7], out_5}), .out_13(out_6), .out_14(out_11),
    .in_4(or_1_out), .out_8(main_1_out_8), .out_9(main_1_out_9), .in_3(ram_1_out_8), .out_11(main_1_out_11),
    .out_12(main_1_out_12), .out_6(main_1_out_6), .in_2(rom_1_out_4), .out_7(main_1_out_7), .out_15(out_10));
  ROM rom_1 (.in_1(main_1_out_6), .in_2(main_1_out_7), .out_4(rom_1_out_4), .in_3(in_2));
  RAM ram_1 (
    .in_1(main_1_out_8), .in_2(main_1_out_9), .in_6(main_1_out_11), .in_7(main_1_out_12),
    .out_8(ram_1_out_8), .in_3(in_2), .in_4(bit_extender_1_out), .in_5(out_11));
  and and_1 (out_8, out_11, in_4);
  assign bit_extender_1_out = {{1{1'b0}}, in_3};  // Bit_Extender bit_extender_1

  assign out_7 = in_2;
  assign out_9 = in_2;
endmodule

module comp (
);

  wire button_1_out, clock_1_out, keyboard_1_avail, proc_1_out_6, proc_1_out_7, proc_1_out_8, proc_1_out_9,
       proc_1_out_10, proc_1_out_11;
  wire [6:0] keyboard_1_data, proc_1_out_5;

  Clock clock_1 (.out(clock_1_out));
  Button button_1 (.out(button_1_out));
  Proc proc_1 (
    .in_2(button_1_out), .out_5(proc_1_out_5), .out_6(proc_1_out_6), .out_7(proc_1_out_7),
    .in_1(clock_1_out), .out_8(proc_1_out_8), .out_9(proc_1_out_9), .in_3(keyboard_1_data),
    .in_4(keyboard_1_avail), .out_10(proc_1_out_10), .out_11(proc_1_out_11));
  LED led_1 (.in(proc_1_out_10));
  TTY #(.rows(16), .cols(64)) tty_1 (.data(proc_1_out_5), .clk(proc_1_out_6), .clr(proc_1_out_7));  // open: we
  LED led_2 (.in(proc_1_out_11));
  Keyboard #(.trigger("falling")) keyboard_1 (
    .clk(proc_1_out_8), .clr(proc_1_out_9), .avail(keyboard_1_avail), .data(keyboard_1_data));  // open: re

  // Notes on the sheet:
  //   Reset Button
  //   Clock
  //   End program indicator
  //   Press reset button, set clock to 0 and press Ctrl+K
  //   License: CC BY-SA 4.0
  //   Author: Kruchinin Tim
  //   Input indicator
endmodule
